# Fritzing sketch ground_station (saved by Fritzing 0.9.3b)
breadboards: 1

parts:
  MCU = Arduino Pro Mini (3.3V)
  XL7105-D03B = IC, SIP package, 9 pins [chip_label=IC]
  BlueSmirf = Bluetooth Mate Silver
  part = smd LED [color="Green (565nm)" package="1206 [SMD]"]
  part_2 = smd LED [color="Yellow (592nm)" package="1206 [SMD]"]
  VCC = Battery block 9V
  B = SWITCH-MOMENTARY-2 [package=tactile-pth-12mm]
  SW = SPST Switch [package=switch-spdt_kit]
  part_3 = Resistor [tolerance=±5% resistance=39 package="0805 [SMD]"]
  part_4 = Resistor [tolerance=±5% resistance=68 package="0805 [SMD]"]

nets:
  N1: MCU.TXO, BlueSmirf.RX_5V
  N2: MCU.RXI, BlueSmirf.TX_5V
  VCC: MCU.VCC, XL7105-D03B.pin9, BlueSmirf.VCC
  GND: MCU.GND, XL7105-D03B.pin7, BlueSmirf.GND, part.cathode, part_2.cathode, VCC.-, B.1
  N3: MCU.RAW, SW.S
  N4: MCU.A1, XL7105-D03B.pin2
  N5: MCU.A0, XL7105-D03B.pin1
  N6: MCU.SCK, XL7105-D03B.pin8
  N7: MCU.MISO, XL7105-D03B.pin4
  N8: MCU.MOSI, XL7105-D03B.pin5
  N9: MCU.D9, XL7105-D03B.pin6
  N10: MCU.D8, B.2
  N11: MCU.D5, part_4.Pin_1
  N12: MCU.D2, part_3.Pin_1
  N13: part.anode, part_3.Pin_0
  N14: part_2.anode, part_4.Pin_0
  N15: VCC.+, SW.P
